# Fritzing sketch racebox_platine_v2_2 (saved by Fritzing 0.9.3b)
circuit board: 18.2702cm x 10.4216cm
breadboards: 1

parts:
  Nano_V3 = Arduino Nano (Rev3.0)
  RX5809 = rounded female pin header, 9 pins [form="♀ (female rounded)"]
  1K = Resistor [tolerance=±5% resistance=220 package=THT]
  1K_2 = Resistor [tolerance=±5% resistance=220 package=THT]
  1k = Resistor [tolerance=±5% resistance=220 package=THT]
  Nano_V4 = Arduino Nano (Rev3.0)
  RX5810 = rounded female pin header, 9 pins [form="♀ (female rounded)"]
  1K1 = Resistor [tolerance=±5% resistance=220 package=THT]
  1K2 = Resistor [tolerance=±5% resistance=220 package=THT]
  1k1 = Resistor [tolerance=±5% resistance=220 package=THT]
  Nano_V5 = Arduino Nano (Rev3.0)
  RX5811 = rounded female pin header, 9 pins [form="♀ (female rounded)"]
  1K3 = Resistor [tolerance=±5% resistance=220 package=THT]
  1K4 = Resistor [tolerance=±5% resistance=220 package=THT]
  1k2 = Resistor [tolerance=±5% resistance=220 package=THT]
  Nano_V6 = Arduino Nano (Rev3.0)
  RX5812 = rounded female pin header, 9 pins [form="♀ (female rounded)"]
  1K5 = Resistor [tolerance=±5% resistance=220 package=THT]
  1K6 = Resistor [tolerance=±5% resistance=220 package=THT]
  1k3 = Resistor [tolerance=±5% resistance=220 package=THT]
  Nano_V3_Master = Arduino Nano (Rev3.0)
  Nano_V7 = Arduino Nano (Rev3.0)
  RX5813 = rounded female pin header, 9 pins [form="♀ (female rounded)"]
  1K7 = Resistor [tolerance=±5% resistance=220 package=THT]
  1K8 = Resistor [tolerance=±5% resistance=220 package=THT]
  1k4 = Resistor [tolerance=±5% resistance=220 package=THT]
  Nano_V8 = Arduino Nano (Rev3.0)
  RX5814 = rounded female pin header, 9 pins [form="♀ (female rounded)"]
  1K9 = Resistor [tolerance=±5% resistance=220 package=THT]
  1K10 = Resistor [tolerance=±5% resistance=220 package=THT]
  1k5 = Resistor [tolerance=±5% resistance=220 package=THT]
  Nano_V9 = Arduino Nano (Rev3.0)
  RX5815 = rounded female pin header, 9 pins [form="♀ (female rounded)"]
  1K11 = Resistor [tolerance=±5% resistance=220 package=THT]
  1K12 = Resistor [tolerance=±5% resistance=220 package=THT]
  1k6 = Resistor [tolerance=±5% resistance=220 package=THT]
  Nano_V10 = Arduino Nano (Rev3.0)
  RX5816 = rounded female pin header, 9 pins [form="♀ (female rounded)"]
  1K13 = Resistor [tolerance=±5% resistance=220 package=THT]
  1K14 = Resistor [tolerance=±5% resistance=220 package=THT]
  1k7 = Resistor [tolerance=±5% resistance=220 package=THT]
  Power_plug1 = Power plug
  U2_-_5V1 = Voltage Regulator [package=sot223]
  R1_330 = Resistor [tolerance=±5% resistance=330 package=THT]
  R2_1k = Resistor [tolerance=±5% resistance=1k package=THT]
  R1_10K = Resistor [tolerance=±5% resistance=10k package=THT]
  R2_110K = Resistor [tolerance=±5% resistance=100k package=THT]

nets:
  N1: Nano_V3.D10, 1K.Pin_0
  N2: Nano_V3.D11/MOSI, 1K_2.Pin_0
  N3: Nano_V3.D12/MISO, 1k.Pin_0
  VIN: Nano_V3.VIN, Nano_V4.VIN, Nano_V5.VIN, Nano_V6.VIN, Nano_V3_Master.VIN, Nano_V7.VIN, Nano_V8.VIN, Nano_V9.VIN, Nano_V10.VIN, R2_1k.Pin_1
  GND: Nano_V3.GND, RX5809.pin4, Nano_V4.GND, RX5810.pin4, Nano_V5.GND, RX5811.pin4, Nano_V6.GND, RX5812.pin4, Nano_V3_Master.GND, Nano_V7.GND, RX5813.pin4, Nano_V8.GND, RX5814.pin4, Nano_V9.GND, RX5815.pin4, Nano_V10.GND, RX5816.pin4, Power_plug1.GND, R1_10K.Pin_0
  N4: Nano_V3.5V, RX5809.pin5
  N5: Nano_V3.A7, RX5809.pin6
  N6: Nano_V3.A5, Nano_V4.A5, Nano_V5.A5, Nano_V6.A5, Nano_V3_Master.A5, Nano_V7.A5, Nano_V8.A5, Nano_V9.A5, Nano_V10.A5
  N7: Nano_V3.A4, Nano_V4.A4, Nano_V5.A4, Nano_V6.A4, Nano_V3_Master.A4, Nano_V7.A4, Nano_V8.A4, Nano_V9.A4, Nano_V10.A4
  N8: RX5809.pin1, 1K.Pin_1
  N9: RX5809.pin2, 1K_2.Pin_1
  N10: RX5809.pin3, 1k.Pin_1
  N11: Nano_V4.D10, 1K1.Pin_0
  N12: Nano_V4.D11/MOSI, 1K2.Pin_0
  N13: Nano_V4.D12/MISO, 1k1.Pin_0
  N14: Nano_V4.5V, RX5810.pin5
  N15: Nano_V4.A7, RX5810.pin6
  N16: RX5810.pin1, 1K1.Pin_1
  N17: RX5810.pin2, 1K2.Pin_1
  N18: RX5810.pin3, 1k1.Pin_1
  N19: Nano_V5.D10, 1K3.Pin_0
  N20: Nano_V5.D11/MOSI, 1K4.Pin_0
  N21: Nano_V5.D12/MISO, 1k2.Pin_0
  N22: Nano_V5.5V, RX5811.pin5
  N23: Nano_V5.A7, RX5811.pin6
  N24: RX5811.pin1, 1K3.Pin_1
  N25: RX5811.pin2, 1K4.Pin_1
  N26: RX5811.pin3, 1k2.Pin_1
  N27: Nano_V6.D10, 1K5.Pin_0
  N28: Nano_V6.D11/MOSI, 1K6.Pin_0
  N29: Nano_V6.D12/MISO, 1k3.Pin_0
  N30: Nano_V6.5V, RX5812.pin5
  N31: Nano_V6.A7, RX5812.pin6
  N32: RX5812.pin1, 1K5.Pin_1
  N33: RX5812.pin2, 1K6.Pin_1
  N34: RX5812.pin3, 1k3.Pin_1
  N35: Nano_V3_Master.A7, R1_10K.Pin_1, R2_110K.Pin_1
  N36: Nano_V7.D10, 1K7.Pin_0
  N37: Nano_V7.D11/MOSI, 1K8.Pin_0
  N38: Nano_V7.D12/MISO, 1k4.Pin_0
  N39: Nano_V7.5V, RX5813.pin5
  N40: Nano_V7.A7, RX5813.pin6
  N41: RX5813.pin1, 1K7.Pin_1
  N42: RX5813.pin2, 1K8.Pin_1
  N43: RX5813.pin3, 1k4.Pin_1
  N44: Nano_V8.D10, 1K9.Pin_0
  N45: Nano_V8.D11/MOSI, 1K10.Pin_0
  N46: Nano_V8.D12/MISO, 1k5.Pin_0
  N47: Nano_V8.5V, RX5814.pin5
  N48: Nano_V8.A7, RX5814.pin6
  N49: RX5814.pin1, 1K9.Pin_1
  N50: RX5814.pin2, 1K10.Pin_1
  N51: RX5814.pin3, 1k5.Pin_1
  N52: Nano_V9.D10, 1K11.Pin_0
  N53: Nano_V9.D11/MOSI, 1K12.Pin_0
  N54: Nano_V9.D12/MISO, 1k6.Pin_0
  N55: Nano_V9.5V, RX5815.pin5
  N56: Nano_V9.A7, RX5815.pin6
  N57: RX5815.pin1, 1K11.Pin_1
  N58: RX5815.pin2, 1K12.Pin_1
  N59: RX5815.pin3, 1k6.Pin_1
  N60: Nano_V10.D10, 1K13.Pin_0
  N61: Nano_V10.D11/MOSI, 1K14.Pin_0
  N62: Nano_V10.D12/MISO, 1k7.Pin_0
  N63: Nano_V10.5V, RX5816.pin5
  N64: Nano_V10.A7, RX5816.pin6
  N65: RX5816.pin1, 1K13.Pin_1
  N66: RX5816.pin2, 1K14.Pin_1
  N67: RX5816.pin3, 1k7.Pin_1
  N68: Power_plug1.VCC, U2_-_5V1.IN, R2_110K.Pin_0
  N69: U2_-_5V1.ADJ, R1_330.Pin_0, R2_1k.Pin_0
  N70: U2_-_5V1.OUT, R1_330.Pin_1

notes:
  CH1
  A4
  A5
  GND
  VIN
  EasyRaceLapTimer RaceBox
  Revision 2.2
  +
  -
